# Fritzing sketch Pi_RGBLED_Common_Anode (saved by Fritzing 0.9.2b)
breadboards: 1

parts:
  Raspberry_Pi1 = Raspberry Pi 2
  LED1 = RGB LED - (4 legs) [package="5 mm [THT]"]
  R1 = Resistor [tolerance=±5% resistance=5.6 package=THT]
  R2 = Resistor [tolerance=±5% resistance=5.6 package=THT]
  R3 = Resistor [tolerance=±5% resistance=68 package=THT]

nets:
  3V3: Raspberry_Pi1.3v3, Raspberry_Pi1.3V3, LED1.common_anode
  N1: Raspberry_Pi1.GPIO17, R3.Pin_1
  N2: Raspberry_Pi1.GPIO22, R1.Pin_1
  N3: Raspberry_Pi1.GPIO18, R2.Pin_1
  N4: LED1.red_cathode, R3.Pin_0
  N5: LED1.green_cathode, R2.Pin_0
  N6: LED1.blue_cathode, R1.Pin_0
